// Logisim project COMP303_TermProject_Hasan_Can_ASLAN_Nursena_KÖPRÜCÜ2.circ as structural Verilog: 7 circuits, main circuit main
module main (
  input  ClearPC,
  input  ClearDataMem,
  input  [31:0] in_3,
  input  ClearReg
);

  wire and_1_out, Clk, comparator_1_eq, comparator_1_lt, comparator_2_eq, controlunit_1_alusrc,
       controlunit_1_blez, controlunit_1_branch, controlunit_1_jump, controlunit_1_memread,
       controlunit_1_memtoreg, controlunit_1_memwrite, controlunit_1_regdst, controlunit_1_regwrite,
       multiplexer_5_out, or_1_out;
  wire [4:0] multiplexer_2_out, rom_1_data_3;
  wire [5:0] opcode;
  wire [15:0] adder_1_out, alu_1_output, multiplexer_1_out, multiplexer_3_out, multiplexer_4_out,
       multiplexer_6_out, n16bitadder_1__16_bit_output, PC_q, ram_1_data, registerfile_1_readdata1,
       registerfile_1_readdata2, rom_1_data, shifter_1_out;
  wire [20:16] rom_1_data_2;

  Multiplexer #(.width(16), .enable("false")) multiplexer_1 (
    .in0(multiplexer_4_out), .in1(rom_1_data), .out(multiplexer_1_out), .sel(controlunit_1_jump));
  Clock clock_1 (.out(Clk));
  Register #(.width(16)) PC (.D(multiplexer_1_out), .Q(PC_q), .clk(Clk), .clr(ClearPC));  // open: en
  _16BitAdder u_16bitadder_1 (
    ._16_bit_X(PC_q), ._16_bit_Y(16'h1), ._16_bit_output(n16bitadder_1__16_bit_output));  // open: Carry_Out, Overflow
  ROM #(.addrWidth(16), .dataWidth(32)) rom_1 (
    .addr(PC_q), .data({opcode, rom_1_data_3, rom_1_data_2, rom_1_data}));  // open: sel
  ControlUnit controlunit_1 (
    .in_1(opcode), .RegDst(controlunit_1_regdst), .Branch(controlunit_1_branch),
    .MemRead(controlunit_1_memread), .MemtoReg(controlunit_1_memtoreg), .Blez(controlunit_1_blez),
    .MemWrite(controlunit_1_memwrite), .ALUSrc(controlunit_1_alusrc), .RegWrite(controlunit_1_regwrite),
    .Jump(controlunit_1_jump));
  Multiplexer #(.width(5), .enable("false")) multiplexer_2 (
    .in0(rom_1_data_2), .in1(rom_1_data[15:11]), .out(multiplexer_2_out), .sel(controlunit_1_regdst));
  RegisterFile registerfile_1 (
    .WriteData(multiplexer_6_out), .WriteEnable(controlunit_1_regwrite), .WriteAddress(multiplexer_2_out),
    .Clk(Clk), .ReadData1(registerfile_1_readdata1), .ReadAddress1(rom_1_data_3),
    .ReadData2(registerfile_1_readdata2), .WriteAddress_2(rom_1_data_2), .Clr(ClearReg));
  Shifter #(.width(16)) shifter_1 (.in(rom_1_data), .\dist (4'b0010), .out(shifter_1_out));
  Adder #(.width(16)) adder_1 (
    .a(n16bitadder_1__16_bit_output), .b(shifter_1_out), .out(adder_1_out));  // open: cin, cout
  Multiplexer #(.width(16), .enable("false")) multiplexer_3 (
    .in0(registerfile_1_readdata2), .in1(rom_1_data), .out(multiplexer_3_out), .sel(controlunit_1_alusrc));
  Multiplexer #(.width(16), .enable("false")) multiplexer_4 (
    .in0(n16bitadder_1__16_bit_output), .in1(adder_1_out), .out(multiplexer_4_out), .sel(and_1_out));
  and and_1 (and_1_out, controlunit_1_branch, multiplexer_5_out);
  Comparator #(.width(5)) comparator_1 (
    .a(rom_1_data_3), .b({5{1'b0}}), .eq(comparator_1_eq), .lt(comparator_1_lt));  // open: gt
  Comparator #(.width(16)) comparator_2 (
    .a(registerfile_1_readdata1), .b(multiplexer_3_out), .eq(comparator_2_eq));  // open: gt, lt
  or or_1 (or_1_out, comparator_1_eq, comparator_1_lt);
  ALU alu_1 (
    .Input_X(registerfile_1_readdata1), .opcode_in(opcode), .Clk(Clk), .Input_Y(multiplexer_3_out),
    .\output (alu_1_output));  // open: zero, carryout, overflow
  Multiplexer #(.enable("false")) multiplexer_5 (
    .in0(comparator_2_eq), .in1(or_1_out), .out(multiplexer_5_out), .sel(controlunit_1_blez));
  RAM #(.addrWidth(16), .dataWidth(16), .bus("separate")) ram_1 (
    .addr(alu_1_output), .din(registerfile_1_readdata2), .data(ram_1_data), .str(controlunit_1_memwrite),
    .clk(Clk), .ld(controlunit_1_memread), .clr(ClearDataMem));  // open: sel
  Multiplexer #(.width(16), .enable("false")) multiplexer_6 (
    .in0(alu_1_output), .in1(ram_1_data), .out(multiplexer_6_out), .sel(controlunit_1_memtoreg));

  // Notes on the sheet:
  //   PC + 4
  //   Instruction Memory
  //   contents of rom_1 (hex, n*v repeats v):
  //   0 14000000 14420004 14a50000 14c60004 14e70008 30020012 28a30000 28c40000 8640000 24000800 18204040
  //   2d010000 14a50001 14c60001 14e70001 14000001 38000006
  //   Jump
  //   RegDst
  //   Branch
  //   MemRead
  //   MemtoReg
  //   Blez
  //   MemWrite
  //   ALUSrc
  //   RegWrite
  //   Sll 2
  //   PCSrc
  //   blez
  //   beq
  //   Data Memory
endmodule

module _1BitAdder (
  input  X,
  input  Y,
  input  Carry_In,
  output Sum,
  output Carry_Out
);

  wire and_1_out, and_2_out, xor_1_out;

  xor xor_1 (xor_1_out, X, Y);
  and and_1 (and_1_out, Carry_In, xor_1_out);
  and and_2 (and_2_out, Y, X);
  xor xor_2 (Sum, xor_1_out, Carry_In);
  or or_1 (Carry_Out, and_1_out, and_2_out);

  // Other names for the same wires on the sheet: C = Carry_In
endmodule

module _16BitAdder (
  input  [15:0] _16_bit_X,
  input  [15:0] _16_bit_Y,
  output [15:0] _16_bit_output,
  output Carry_Out,
  output Overflow
);

  wire n1bitadder_1_carry_out, n1bitadder_2_carry_out, n1bitadder_3_carry_out, n1bitadder_4_carry_out,
       n1bitadder_5_carry_out, n1bitadder_6_carry_out, n1bitadder_7_carry_out, n1bitadder_8_carry_out,
       n1bitadder_9_carry_out, n1bitadder_10_carry_out, n1bitadder_11_carry_out, n1bitadder_12_carry_out,
       n1bitadder_13_carry_out, n1bitadder_14_carry_out, n1bitadder_15_carry_out, xor_1_out, xor_2_out;

  _1BitAdder u_1bitadder_1 (
    .X(_16_bit_X[0]), .Y(_16_bit_Y[0]), .Carry_In(1'b0), .Sum(_16_bit_output[0]),
    .Carry_Out(n1bitadder_1_carry_out));
  _1BitAdder u_1bitadder_2 (
    .X(_16_bit_X[1]), .Y(_16_bit_Y[1]), .Carry_In(n1bitadder_1_carry_out), .Sum(_16_bit_output[1]),
    .Carry_Out(n1bitadder_2_carry_out));
  _1BitAdder u_1bitadder_3 (
    .X(_16_bit_X[2]), .Y(_16_bit_Y[2]), .Carry_In(n1bitadder_2_carry_out), .Sum(_16_bit_output[2]),
    .Carry_Out(n1bitadder_3_carry_out));
  _1BitAdder u_1bitadder_4 (
    .X(_16_bit_X[3]), .Y(_16_bit_Y[3]), .Carry_In(n1bitadder_3_carry_out), .Sum(_16_bit_output[3]),
    .Carry_Out(n1bitadder_4_carry_out));
  _1BitAdder u_1bitadder_5 (
    .X(_16_bit_X[4]), .Y(_16_bit_Y[4]), .Carry_In(n1bitadder_4_carry_out), .Sum(_16_bit_output[4]),
    .Carry_Out(n1bitadder_5_carry_out));
  _1BitAdder u_1bitadder_6 (
    .X(_16_bit_X[5]), .Y(_16_bit_Y[5]), .Carry_In(n1bitadder_5_carry_out), .Sum(_16_bit_output[5]),
    .Carry_Out(n1bitadder_6_carry_out));
  _1BitAdder u_1bitadder_7 (
    .X(_16_bit_X[6]), .Y(_16_bit_Y[6]), .Carry_In(n1bitadder_6_carry_out), .Sum(_16_bit_output[6]),
    .Carry_Out(n1bitadder_7_carry_out));
  _1BitAdder u_1bitadder_8 (
    .X(_16_bit_X[7]), .Y(_16_bit_Y[7]), .Carry_In(n1bitadder_7_carry_out), .Sum(_16_bit_output[7]),
    .Carry_Out(n1bitadder_8_carry_out));
  _1BitAdder u_1bitadder_9 (
    .X(_16_bit_X[8]), .Y(_16_bit_Y[8]), .Carry_In(n1bitadder_8_carry_out), .Sum(_16_bit_output[8]),
    .Carry_Out(n1bitadder_9_carry_out));
  _1BitAdder u_1bitadder_10 (
    .X(_16_bit_X[9]), .Y(_16_bit_Y[9]), .Carry_In(n1bitadder_9_carry_out), .Sum(_16_bit_output[9]),
    .Carry_Out(n1bitadder_10_carry_out));
  _1BitAdder u_1bitadder_11 (
    .X(_16_bit_X[10]), .Y(_16_bit_Y[10]), .Carry_In(n1bitadder_10_carry_out), .Sum(_16_bit_output[10]),
    .Carry_Out(n1bitadder_11_carry_out));
  _1BitAdder u_1bitadder_12 (
    .X(_16_bit_X[11]), .Y(_16_bit_Y[11]), .Carry_In(n1bitadder_11_carry_out), .Sum(_16_bit_output[11]),
    .Carry_Out(n1bitadder_12_carry_out));
  _1BitAdder u_1bitadder_13 (
    .X(_16_bit_X[12]), .Y(_16_bit_Y[12]), .Carry_In(n1bitadder_12_carry_out), .Sum(_16_bit_output[12]),
    .Carry_Out(n1bitadder_13_carry_out));
  _1BitAdder u_1bitadder_14 (
    .X(_16_bit_X[13]), .Y(_16_bit_Y[13]), .Carry_In(n1bitadder_13_carry_out), .Sum(_16_bit_output[13]),
    .Carry_Out(n1bitadder_14_carry_out));
  _1BitAdder u_1bitadder_15 (
    .X(_16_bit_X[14]), .Y(_16_bit_Y[14]), .Carry_In(n1bitadder_14_carry_out), .Sum(_16_bit_output[14]),
    .Carry_Out(n1bitadder_15_carry_out));
  _1BitAdder u_1bitadder_16 (
    .X(_16_bit_X[15]), .Y(_16_bit_Y[15]), .Carry_In(n1bitadder_15_carry_out), .Sum(_16_bit_output[15]),
    .Carry_Out(Carry_Out));
  xor xor_1 (xor_1_out, _16_bit_X[15], _16_bit_Y[15]);
  xor xor_2 (xor_2_out, _16_bit_output[15], _16_bit_X[15]);
  Multiplexer #(.enable("false")) multiplexer_1 (.in0(xor_2_out), .in1(1'b0), .out(Overflow), .sel(xor_1_out));
endmodule

module RegisterFile (
  input  [15:0] WriteData,
  input  WriteEnable,
  input  [4:0] WriteAddress,
  input  [4:0] ReadAddress1,
  input  Clk,
  input  Clr,
  input  [4:0] WriteAddress_2,
  output [15:0] ReadData1,
  output [15:0] ReadData2
);

  wire and_1_out, and_2_out, and_3_out, and_4_out, and_5_out, and_6_out, and_7_out, and_8_out, and_9_out,
       and_10_out, and_11_out, and_12_out, and_13_out, and_14_out, and_15_out, and_16_out,
       demultiplexer_1_out0, demultiplexer_1_out1, demultiplexer_1_out2, demultiplexer_1_out3,
       demultiplexer_2_out0, demultiplexer_2_out1, demultiplexer_2_out2, demultiplexer_2_out3;
  wire [15:0] register_1_q, register_2_q, register_3_q, register_4_q, register_5_q, register_6_q,
       register_7_q, register_8_q, register_9_q, register_10_q, register_11_q, register_12_q, register_13_q,
       register_14_q, register_15_q, register_16_q;

  Demultiplexer #(.select(2)) demultiplexer_1 (
    .out0(demultiplexer_1_out0), .out1(demultiplexer_1_out1), .out2(demultiplexer_1_out2),
    .out3(demultiplexer_1_out3), .in(WriteEnable), .sel(WriteAddress[3:2]));  // open: en
  and and_1 (and_1_out, demultiplexer_2_out0, demultiplexer_1_out0);
  and and_2 (and_2_out, demultiplexer_2_out0, demultiplexer_1_out1);
  and and_3 (and_3_out, demultiplexer_2_out0, demultiplexer_1_out2);
  and and_4 (and_4_out, demultiplexer_2_out0, demultiplexer_1_out3);
  Register #(.width(16)) register_1 (.D(WriteData), .en(and_1_out), .Q(register_1_q), .clk(Clk), .clr(Clr));
  Register #(.width(16)) register_2 (.D(WriteData), .en(and_2_out), .Q(register_2_q), .clk(Clk), .clr(Clr));
  Register #(.width(16)) register_3 (.D(WriteData), .en(and_3_out), .Q(register_3_q), .clk(Clk), .clr(Clr));
  Register #(.width(16)) register_4 (.D(WriteData), .en(and_4_out), .Q(register_4_q), .clk(Clk), .clr(Clr));
  Demultiplexer #(.select(2)) demultiplexer_2 (
    .out0(demultiplexer_2_out0), .out1(demultiplexer_2_out1), .out2(demultiplexer_2_out2),
    .out3(demultiplexer_2_out3), .sel(WriteAddress[1:0]));  // open: in, en
  and and_5 (and_5_out, demultiplexer_2_out1, demultiplexer_1_out0);
  and and_6 (and_6_out, demultiplexer_2_out1, demultiplexer_1_out1);
  and and_7 (and_7_out, demultiplexer_2_out1, demultiplexer_1_out2);
  and and_8 (and_8_out, demultiplexer_2_out1, demultiplexer_1_out3);
  and and_9 (and_9_out, demultiplexer_2_out2, demultiplexer_1_out0);
  Register #(.width(16)) register_5 (.D(WriteData), .en(and_5_out), .Q(register_5_q), .clk(Clk), .clr(Clr));
  and and_10 (and_10_out, demultiplexer_2_out2, demultiplexer_1_out1);
  Register #(.width(16)) register_6 (.D(WriteData), .en(and_6_out), .Q(register_6_q), .clk(Clk), .clr(Clr));
  and and_11 (and_11_out, demultiplexer_2_out2, demultiplexer_1_out2);
  Register #(.width(16)) register_7 (.D(WriteData), .en(and_7_out), .Q(register_7_q), .clk(Clk), .clr(Clr));
  and and_12 (and_12_out, demultiplexer_2_out2, demultiplexer_1_out3);
  Register #(.width(16)) register_8 (.D(WriteData), .en(and_8_out), .Q(register_8_q), .clk(Clk), .clr(Clr));
  Register #(.width(16)) register_9 (.D(WriteData), .en(and_9_out), .Q(register_9_q), .clk(Clk), .clr(Clr));
  Register #(.width(16)) register_10 (.D(WriteData), .en(and_10_out), .Q(register_10_q), .clk(Clk), .clr(Clr));
  Register #(.width(16)) register_11 (.D(WriteData), .en(and_11_out), .Q(register_11_q), .clk(Clk), .clr(Clr));
  Register #(.width(16)) register_12 (.D(WriteData), .en(and_12_out), .Q(register_12_q), .clk(Clk), .clr(Clr));
  and and_13 (and_13_out, demultiplexer_2_out3, demultiplexer_1_out0);
  Register #(.width(16)) register_13 (.D(WriteData), .en(and_13_out), .Q(register_13_q), .clk(Clk), .clr(Clr));
  and and_14 (and_14_out, demultiplexer_2_out3, demultiplexer_1_out1);
  Register #(.width(16)) register_14 (.D(WriteData), .en(and_14_out), .Q(register_14_q), .clk(Clk), .clr(Clr));
  and and_15 (and_15_out, demultiplexer_2_out3, demultiplexer_1_out2);
  Register #(.width(16)) register_15 (.D(WriteData), .en(and_15_out), .Q(register_15_q), .clk(Clk), .clr(Clr));
  and and_16 (and_16_out, demultiplexer_2_out3, demultiplexer_1_out3);
  Register #(.width(16)) register_16 (.D(WriteData), .en(and_16_out), .Q(register_16_q), .clk(Clk), .clr(Clr));
  Multiplexer #(.select(4), .width(16)) multiplexer_1 (
    .in0(register_1_q), .in1(register_5_q), .in2(register_9_q), .in3(register_13_q), .in4(register_2_q),
    .in5(register_6_q), .in6(register_10_q), .in7(register_14_q), .in8(register_3_q), .in9(register_7_q),
    .in10(register_11_q), .in11(register_15_q), .in12(register_4_q), .in13(register_8_q),
    .in14(register_12_q), .in15(register_16_q), .out(ReadData1), .sel(ReadAddress1[3:0]));  // open: en
  Multiplexer #(.select(4), .width(16)) multiplexer_2 (
    .in0(register_1_q), .in1(register_5_q), .in2(register_9_q), .in3(register_13_q), .in4(register_2_q),
    .in5(register_6_q), .in6(register_10_q), .in7(register_14_q), .in8(register_3_q), .in9(register_7_q),
    .in10(register_11_q), .in11(register_15_q), .in12(register_4_q), .in13(register_8_q),
    .in14(register_12_q), .in15(register_16_q), .out(ReadData2), .sel(WriteAddress_2[3:0]));  // open: en
endmodule

module ALU (
  input  [15:0] Input_X,
  input  [5:0] opcode_in,
  input  Clk,
  input  [15:0] Input_Y,
  output zero,
  output carryout,
  output overflow,
  output [15:0] \output 
);

  wire borrow_out_sub, carryout_add, carryout_addi, comparator_1_lt, comparator_2_eq, overflow_add,
       overflow_addi;
  wire [15:0] Add__16_bit_output, Addi_2__16_bit_output, Addi_3__16_bit_output, Addi__16_bit_output, And_out,
       bit_extender_1_out, demultiplexer_1_out0, demultiplexer_1_out1, demultiplexer_1_out2,
       demultiplexer_1_out3, demultiplexer_1_out4, demultiplexer_1_out5, demultiplexer_1_out6,
       demultiplexer_1_out7, demultiplexer_1_out10, demultiplexer_1_out11, demultiplexer_1_out15,
       demultiplexer_2_out0, demultiplexer_2_out1, demultiplexer_2_out2, demultiplexer_2_out3,
       demultiplexer_2_out4, demultiplexer_2_out5, demultiplexer_2_out6, demultiplexer_2_out7,
       demultiplexer_2_out10, demultiplexer_2_out11, Hi_q, Lo_q, multiplexer_1_out, multiplier_1_cout,
       multiplier_1_out, MyIns_flipped, Or_out, shifter_1_out, subtractor_1_out;

  Demultiplexer #(.select(4), .width(16), .enable("false")) demultiplexer_1 (
    .out0(demultiplexer_1_out0), .out1(demultiplexer_1_out1), .out2(demultiplexer_1_out2),
    .out3(demultiplexer_1_out3), .out4(demultiplexer_1_out4), .out5(demultiplexer_1_out5),
    .out6(demultiplexer_1_out6), .out7(demultiplexer_1_out7), .out10(demultiplexer_1_out10),
    .out11(demultiplexer_1_out11), .out15(demultiplexer_1_out15), .in(Input_X), .sel(opcode_in[3:0]));  // open: out8, out9, out12, out13, out14
  Demultiplexer #(.select(4), .width(16), .enable("false")) demultiplexer_2 (
    .out0(demultiplexer_2_out0), .out1(demultiplexer_2_out1), .out2(demultiplexer_2_out2),
    .out3(demultiplexer_2_out3), .out4(demultiplexer_2_out4), .out5(demultiplexer_2_out5),
    .out6(demultiplexer_2_out6), .out7(demultiplexer_2_out7), .out10(demultiplexer_2_out10),
    .out11(demultiplexer_2_out11), .in(Input_Y), .sel(opcode_in[3:0]));  // open: out8, out9, out12, out13, out14, out15
  _16BitAdder Add (
    ._16_bit_X(demultiplexer_1_out0), ._16_bit_Y(demultiplexer_2_out0), ._16_bit_output(Add__16_bit_output),
    .Carry_Out(carryout_add), .Overflow(overflow_add));
  Subtractor #(.width(16)) subtractor_1 (
    .a(demultiplexer_1_out1), .b(demultiplexer_2_out1), .out(subtractor_1_out), .bout(borrow_out_sub));  // open: bin
  Multiplier #(.width(16)) multiplier_1 (
    .a(demultiplexer_1_out2), .b(demultiplexer_2_out2), .out(multiplier_1_out), .cout(multiplier_1_cout));  // open: cin
  _16BitAdder Addi (
    ._16_bit_X(demultiplexer_1_out5), ._16_bit_Y(demultiplexer_2_out5), ._16_bit_output(Addi__16_bit_output),
    .Carry_Out(carryout_addi), .Overflow(overflow_addi));
  Shifter #(.width(16)) shifter_1 (.in(demultiplexer_1_out6), .\dist (demultiplexer_2_out6[9:6]), .out(shifter_1_out));
  Comparator #(.width(16)) comparator_1 (
    .a(demultiplexer_1_out7), .b(demultiplexer_2_out7), .lt(comparator_1_lt));  // open: gt, eq
  myIns MyIns (.Input(demultiplexer_1_out15), .opcode(opcode_in[3:0]), .Flipped(MyIns_flipped));
  _16BitAdder Addi_2 (
    ._16_bit_X(demultiplexer_1_out10), ._16_bit_Y(demultiplexer_2_out10),
    ._16_bit_output(Addi_2__16_bit_output));  // open: Carry_Out, Overflow
  _16BitAdder Addi_3 (
    ._16_bit_X(demultiplexer_1_out11), ._16_bit_Y(demultiplexer_2_out11),
    ._16_bit_output(Addi_3__16_bit_output));  // open: Carry_Out, Overflow
  Comparator #(.width(4)) comparator_2 (.a(opcode_in[3:0]), .b(4'b0010), .eq(comparator_2_eq));  // open: gt, lt
  assign And_out = demultiplexer_1_out3 & demultiplexer_2_out3;  // AND_Gate And, 16 bits wide
  assign Or_out = demultiplexer_1_out4 | demultiplexer_2_out4;  // OR_Gate Or, 16 bits wide
  assign bit_extender_1_out = {{15{1'b0}}, comparator_1_lt};  // Bit_Extender bit_extender_1
  Register #(.width(16)) Lo (.D(multiplier_1_out), .en(comparator_2_eq), .Q(Lo_q), .clk(Clk));  // open: clr
  Register #(.width(16)) Hi (.D(multiplier_1_cout), .en(comparator_2_eq), .Q(Hi_q), .clk(Clk));  // open: clr
  Multiplexer #(.select(4), .width(16)) multiplexer_1 (
    .in0({16{1'b0}}), .in1({16{1'b0}}), .in2({16{1'b0}}), .in3({16{1'b0}}), .in4({16{1'b0}}),
    .in5({16{1'b0}}), .in6({16{1'b0}}), .in7({16{1'b0}}), .in8(Hi_q), .in9(Lo_q), .in10({16{1'b0}}),
    .in11({16{1'b0}}), .in12({16{1'b0}}), .in13({16{1'b0}}), .in14({16{1'b0}}), .in15({16{1'b0}}),
    .out(multiplexer_1_out), .sel(opcode_in[3:0]));  // open: en
  Comparator #(.width(16)) comparator_3 (.a(\output ), .b({16{1'b0}}), .eq(zero));  // open: gt, lt
  or or_2 (carryout, carryout_add, carryout_addi);
  or or_3 (overflow, overflow_add, overflow_addi);
  assign \output  = Addi_2__16_bit_output | bit_extender_1_out | shifter_1_out | Addi__16_bit_output | Or_out | MyIns_flipped | And_out | multiplexer_1_out | subtractor_1_out | Add__16_bit_output | Addi_3__16_bit_output;  // OR_Gate or_4, 16 bits wide

  // Other names for the same wires on the sheet: opcode[3:0] = opcode_in[3:0]; output_t[15:0] = \output 
endmodule

module ControlUnit (
  input  [5:0] in_1,
  output RegDst,
  output Branch,
  output MemRead,
  output MemtoReg,
  output Blez,
  output MemWrite,
  output ALUSrc,
  output RegWrite,
  output Jump
);

  wire decoder_1_out0, decoder_1_out1, decoder_1_out3, decoder_1_out4, decoder_1_out5, decoder_1_out6,
       decoder_1_out7, decoder_1_out8, decoder_1_out9, decoder_1_out12, decoder_1_out15;

  Decoder #(.select(5), .enable("false")) decoder_1 (
    .out0(decoder_1_out0), .out1(decoder_1_out1), .out3(decoder_1_out3), .out4(decoder_1_out4),
    .out5(decoder_1_out5), .out6(decoder_1_out6), .out7(decoder_1_out7), .out8(decoder_1_out8),
    .out9(decoder_1_out9), .out10(MemRead), .out11(MemWrite), .out12(decoder_1_out12), .out13(Blez),
    .out14(Jump), .out15(decoder_1_out15), .sel(in_1[4:0]));  // open: out2, out16, out17, out18, out19, out20, out21, out22, out23, out24, out25, out26, out27, out28, out29, out30, out31
  or or_1 (RegDst, decoder_1_out6, decoder_1_out9, decoder_1_out8, decoder_1_out7, decoder_1_out4, decoder_1_out3, decoder_1_out1, decoder_1_out0);
  or or_2 (Branch, Blez, decoder_1_out12);
  or or_3 (ALUSrc, MemRead, decoder_1_out6, decoder_1_out5, MemWrite);
  or or_4 (RegWrite, decoder_1_out0, decoder_1_out1, decoder_1_out3, decoder_1_out4, decoder_1_out5, decoder_1_out6, decoder_1_out7, MemRead, decoder_1_out8, decoder_1_out9, decoder_1_out15);

  assign MemtoReg = MemRead;
endmodule

module myIns (
  input  [15:0] Input,
  input  [3:0] opcode,
  output [15:0] Flipped
);

  wire comparator_1_eq;
  wire [15:0] not_1_out;

  not not_1 (not_1_out[0], Input[0]);
  not not_2 (not_1_out[1], Input[1]);
  not not_3 (not_1_out[2], Input[2]);
  not not_4 (not_1_out[3], Input[3]);
  not not_5 (not_1_out[4], Input[4]);
  not not_6 (not_1_out[5], Input[5]);
  not not_7 (not_1_out[6], Input[6]);
  not not_8 (not_1_out[7], Input[7]);
  not not_9 (not_1_out[8], Input[8]);
  not not_10 (not_1_out[9], Input[9]);
  not not_11 (not_1_out[10], Input[10]);
  not not_12 (not_1_out[11], Input[11]);
  not not_13 (not_1_out[12], Input[12]);
  not not_14 (not_1_out[13], Input[13]);
  not not_15 (not_1_out[14], Input[14]);
  not not_16 (not_1_out[15], Input[15]);
  Comparator #(.width(4), .mode("unsigned")) comparator_1 (
    .a(opcode), .b(4'b1111), .eq(comparator_1_eq));  // open: gt, lt
  Multiplexer #(.width(16), .enable("false")) multiplexer_1 (
    .in0({16{1'b0}}), .in1(not_1_out), .out(Flipped), .sel(comparator_1_eq));
endmodule
